// Logisim project Adders.circ as structural Verilog: 5 circuits, main circuit FullAdder
module FullAdder (
  input  A,
  input  B,
  input  C_in,
  output Sum,
  output C_out
);

  wire halfadder_1_carry, halfadder_1_sum, halfadder_2_carry;

  HalfAdder halfadder_1 (.A(A), .B(B), .Sum(halfadder_1_sum), .Carry(halfadder_1_carry));
  HalfAdder halfadder_2 (.A(halfadder_1_sum), .B(C_in), .Sum(Sum), .Carry(halfadder_2_carry));
  or or_1 (C_out, halfadder_2_carry, halfadder_1_carry);
endmodule

module HalfAdder (
  input  A,
  input  B,
  output Sum,
  output Carry
);

  xor xor_1 (Sum, A, B);
  and and_1 (Carry, A, B);
endmodule

module FourBitAdder (
  input  [3:0] A,
  input  [3:0] B,
  output [3:0] Sum,
  output C_out
);

  wire fulladder_1_c_out, fulladder_2_c_out, fulladder_3_c_out, undriven;

  // NoConnect on undriven
  FullAdder fulladder_1 (.A(A[0]), .B(B[0]), .C_in(undriven), .Sum(Sum[0]), .C_out(fulladder_1_c_out));
  FullAdder fulladder_2 (.A(A[1]), .B(B[1]), .C_in(fulladder_1_c_out), .Sum(Sum[1]), .C_out(fulladder_2_c_out));
  FullAdder fulladder_3 (.A(A[2]), .B(B[2]), .C_in(fulladder_2_c_out), .Sum(Sum[2]), .C_out(fulladder_3_c_out));
  FullAdder fulladder_4 (.A(A[3]), .B(B[3]), .C_in(fulladder_3_c_out), .Sum(Sum[3]), .C_out(C_out));
endmodule

module ALU (
  input  A,
  input  B,
  input  Opcode,
  output Result
);

  wire and_1_out, fulladder_1_c_out, fulladder_1_sum;

  and and_1 (and_1_out, A, B);
  FullAdder fulladder_1 (.A(A), .B(B), .Sum(fulladder_1_sum), .C_out(fulladder_1_c_out));  // open: C_in
  // NoConnect on fulladder_1_c_out
  Mux mux_1 (.A(fulladder_1_sum), .B(and_1_out), .Sel(Opcode), .Result(Result));
endmodule

module Mux (
  input  A,
  input  B,
  input  Sel,
  output Result
);

  wire and_1_out, and_2_out, not_1_out;

  not not_1 (not_1_out, Sel);
  and and_1 (and_1_out, A, not_1_out);
  and and_2 (and_2_out, B, Sel);
  or or_1 (Result, and_1_out, and_2_out);
endmodule
